# Fritzing sketch Reproductor_mp3_irRemote (saved by Fritzing 0.9.3b)
circuit board: 8.46667cm x 5.64444cm
breadboards: 1

parts:
  Componente1 = Arduino Nano (Rev3.0)
  DFRobot_DFPlayer_Mini1 = DFRobot DFPlayer Mini [part_number=DFR0299]
  Mod1 = KY-022 Infrared Receiver Module [package="Breakout board"]
  Display1 = LCD screen 16x2 IIC [part_number=101290]
  SP1 = SPEAKER [package=pcb_mount_speaker]
  R1 = Resistor [tolerance=±5% resistance=1k package="0805 [SMD]"]
  LED1 = smd LED [color="Red (633nm)" package="0805 [SMD]"]
  R2 = Resistor [tolerance=±5% resistance=220 package="0805 [SMD]"]
  X1 = USB Connectors [package=usb-a-s-nosilk]

nets:
  GND: Componente1.GND, DFRobot_DFPlayer_Mini1.GND-1, DFRobot_DFPlayer_Mini1.GND-2, Mod1.-, Display1.GND, R2.Pin_0, X1.GND
  N1: Componente1.D2, Mod1.S
  N2: Componente1.D3, LED1.anode
  N3: Componente1.D10, DFRobot_DFPlayer_Mini1.TX
  N4: Componente1.D11/MOSI, R1.Pin_0
  VCC: Componente1.5V, DFRobot_DFPlayer_Mini1.VCC, Mod1.Vin, Display1.VCC, X1.VBUS
  N5: Componente1.A5, Display1.SCL
  N6: Componente1.A4, Display1.SDA
  N7: DFRobot_DFPlayer_Mini1.RX, R1.Pin_1
  N8: DFRobot_DFPlayer_Mini1.SPK_1, SP1.-
  N9: DFRobot_DFPlayer_Mini1.SPK_2, SP1.+
  N10: DFRobot_DFPlayer_Mini1.USB_POS, X1.D+
  N11: DFRobot_DFPlayer_Mini1.USB_NEG, X1.D-
  N12: LED1.cathode, R2.Pin_1

custom parts:
  KY-022 Infrared Receiver Module: KY-022 IR receiver module, reacts to 38kHz infrared light.
  LCD screen 16x2 IIC: LCD screen with HD44780 controller enables showing text, symbols, value or anything else that comes from Croduino/Arduino. It is capable of showing 16 symbols in two lines and therefore can be used in many projects that need to send clearly visible and legible output information.. • Color of symbols: White • Backlight: Blue • Dimensions: 80 x 36 x 12 mm • Screen dimensions: 64.5 x 16 mm •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
